// Logisim project B22CS068.circ as structural Verilog: 10 circuits, main circuit main
module main (
  input  in_1,
  input  [31:0] in_2,
  input  [4:0] in_3,
  input  [7:0] in_4,
  input  in_5,
  output RegDst,
  output NO_OP,
  output ALUSrc,
  output ADD,
  output SUB,
  output MemtoReg,
  output AND,
  output RegWrite,
  output OR,
  output Memread,
  output SLT,
  output MemWrite,
  output NOR,
  output Branch,
  output ALUOp_1,
  output ALUOp_0,
  output Jump,
  output [31:0] Output,
  output Over_flow
);

  wire ALU_Control__0, ALU_Control__1, ALU_Control__2, clk, not_1_out, or_1_out;
  wire [4:0] multiplexer_1_out, Rd, Rs, Rt;
  wire [5:0] func, op_code;
  wire [7:0] adder_1_out, PC_q;
  wire [10:6] ram_1_data;
  wire [31:0] multiplexer_2_out, register_set_1_rs_2, register_set_1_rt_2, Rs_q, Rt_q;

  Clock clock (.out(clk));
  CONTROL Control (
    .op_5(op_code[5]), .op_4(op_code[4]), .op_3(op_code[3]), .op_2(op_code[2]), .op_1(op_code[1]),
    .op_0(op_code[0]), .RegDst(RegDst), .ALUSrc(ALUSrc), .MemtoReg(MemtoReg), .RegWrite(RegWrite),
    .Memread(Memread), .MemWrite(MemWrite), .Branch(Branch), .ALUOp_1(ALUOp_1), .ALUOp_0(ALUOp_0), .jump(Jump));
  Multiplexer #(.width(5), .enable("false")) multiplexer_1 (.in0(Rd), .in1(in_3), .out(multiplexer_1_out), .sel(in_1));
  or or_1 (or_1_out, RegWrite, in_1);
  Multiplexer #(.width(32), .enable("false")) multiplexer_2 (
    .in0(Output), .in1(in_2), .out(multiplexer_2_out), .sel(in_1));
  Register_set register_set_1 (
    .Rs(Rs), .Rt(Rt), .Rd(multiplexer_1_out), .W_bus(multiplexer_2_out), .RegWrite(or_1_out),
    .Clock(not_1_out), .Rs_2(register_set_1_rs_2), .Rt_2(register_set_1_rt_2));
  not not_1 (not_1_out, clk);
  ALUCONTROL ALU_Control (
    .fun_3(func[5]), .fun_4(func[4]), .fun_3_2(func[3]), .fun_2(func[2]), .fun_1(func[1]), .fun_0(func[0]),
    .MUX_1(ALUOp_1), .MUX_0(ALUOp_0), ._2(ALU_Control__2), ._1(ALU_Control__1), .JUMP(Jump),
    ._0(ALU_Control__0), .NO_OP(NO_OP), .ADD(ADD), .SUB(SUB), .AND(AND), .OR(OR), .SLT(SLT), .NOR(NOR));
  Register #(.width(32), .trigger("high")) u_Rs (.D(register_set_1_rs_2), .en(1'b1), .Q(Rs_q), .clk(clk));  // open: clr
  Register #(.width(32), .trigger("high")) u_Rt (.D(register_set_1_rt_2), .en(1'b1), .Q(Rt_q), .clk(clk));  // open: clr
  Register #(.width(32), .trigger("high")) u_Rd (.en(1'b1), .clk(clk));  // open: D, Q, clr
  // Probe on Rs_q
  // Probe on Rt_q
  ALU alu_1 (
    .A(Rt_q), .B(Rs_q), .over_flow(Over_flow), .\output (Output), ._0(ALU_Control__0), ._1(ALU_Control__1),
    ._2(ALU_Control__2));
  Register PC (.D(adder_1_out), .en(1'b1), .Q(PC_q), .clk(clk), .clr(in_5));
  // Probe on Output
  Adder adder_1 (.a(in_4), .b(PC_q), .out(adder_1_out));  // open: cin, cout
  RAM #(.dataWidth(32), .bus("separate")) ram_1 (
    .addr(PC_q), .data({op_code, Rs, Rt, Rd, ram_1_data, func}), .str(1'b0), .clk(1'b0), .ld(1'b1));  // open: din, sel, clr

  // Other names for the same wires on the sheet: load = in_1; load_data[31:0] = in_2; load_register[4:0] = in_3

  // Notes on the sheet:
  //   MIPS processor for R-Type instructions
  //   Instruction decoding
  //   ALU
  //   Write back
  //   Instruction memory
  //   Instruction fetching
endmodule

module CONTROL (
  input  op_5,
  input  op_4,
  input  op_3,
  input  op_2,
  input  op_1,
  input  op_0,
  output RegDst,
  output ALUSrc,
  output MemtoReg,
  output RegWrite,
  output Memread,
  output MemWrite,
  output Branch,
  output ALUOp_1,
  output ALUOp_0,
  output jump
);

  wire and_2_out, and_4_out, and_5_out, and_6_out, and_10_out, and_11_out, and_12_out, not_1_out, not_2_out,
       not_3_out, not_4_out, not_5_out, not_6_out, not_7_out;

  not not_1 (not_1_out, op_5);
  not not_2 (not_2_out, op_4);
  not not_3 (not_3_out, op_3);
  not not_4 (not_4_out, op_2);
  not not_5 (not_5_out, op_1);
  not not_6 (not_6_out, op_0);
  not not_7 (not_7_out, 1'b1);
  and and_1 (RegDst, not_3_out, not_4_out, not_5_out);
  and and_2 (and_2_out, not_4_out, op_0);
  and and_3 (MemtoReg, op_5, not_3_out);
  and and_4 (and_4_out, not_4_out, not_5_out);
  and and_5 (and_5_out, not_1_out, op_3);
  and and_6 (and_6_out, not_3_out, not_4_out, op_0);
  and and_7 (Memread, op_5, not_3_out);
  and and_8 (MemWrite, op_5, op_3);
  and and_9 (Branch, not_3_out, op_2);
  and and_10 (and_10_out, not_3_out, not_4_out, not_5_out);
  and and_11 (and_11_out, not_1_out, op_3, op_1);
  and and_12 (and_12_out, op_3, op_2);
  and and_13 (jump, not_1_out, not_3_out, op_1);
  or or_1 (ALUSrc, op_3, and_2_out);
  or or_2 (RegWrite, and_4_out, and_5_out, and_6_out);
  or or_3 (ALUOp_1, and_10_out, and_11_out, and_12_out);

  assign ALUOp_0 = op_2;
endmodule

module ALUCONTROL (
  input  fun_3,
  input  fun_4,
  input  fun_3_2,
  input  fun_2,
  input  fun_1,
  input  fun_0,
  input  JUMP,
  input  MUX_1,
  input  MUX_0,
  output NO_OP,
  output ADD,
  output SUB,
  output AND,
  output OR,
  output _2,
  output _1,
  output _0,
  output SLT,
  output NOR
);

  wire and_1_out, and_3_out, and_4_out, not_1_out, not_2_out, not_3_out, not_4_out, not_5_out, not_6_out,
       not_7_out, not_8_out, not_9_out, not_10_out, not_11_out, not_12_out, not_13_out, not_14_out,
       not_15_out, not_16_out, or_3_out;
  wire [3:0] multiplexer_1_out;

  Multiplexer #(.select(2), .width(4), .enable("false")) multiplexer_1 (
    .in0(4'b0000), .in1(4'b0010), .in2({fun_3_2, fun_2, fun_1, fun_0}), .in3(4'b0000),
    .out(multiplexer_1_out), .sel({MUX_1, MUX_0}));
  and and_1 (and_1_out, multiplexer_1_out[2], multiplexer_1_out[1]);
  not not_1 (not_1_out, multiplexer_1_out[1]);
  not not_2 (not_2_out, multiplexer_1_out[3]);
  or or_1 (_2, and_1_out, multiplexer_1_out[3]);
  and and_2 (_1, multiplexer_1_out[2], not_1_out);
  and and_3 (and_3_out, not_2_out, multiplexer_1_out[1]);
  not not_3 (not_3_out, _2);
  not not_4 (not_4_out, _1);
  or or_2 (_0, multiplexer_1_out[0], and_3_out);
  or or_3 (or_3_out, not_3_out, not_4_out);
  and and_4 (and_4_out, or_3_out, not_5_out);
  not not_5 (not_5_out, JUMP);
  not not_6 (not_6_out, _2);
  not not_7 (not_7_out, _1);
  not not_8 (not_8_out, _0);
  not not_9 (not_9_out, _2);
  not not_10 (not_10_out, _1);
  not not_11 (not_11_out, _2);
  not not_12 (not_12_out, _0);
  not not_13 (not_13_out, _2);
  not not_14 (not_14_out, _1);
  not not_15 (not_15_out, _0);
  not not_16 (not_16_out, _1);
  not not_17 (NO_OP, and_4_out);
  and and_5 (ADD, not_6_out, not_7_out, and_4_out, not_8_out);
  and and_6 (SUB, not_9_out, not_10_out, and_4_out, _0);
  and and_7 (AND, not_11_out, _1, not_12_out, and_4_out);
  and and_8 (OR, not_13_out, _1, _0, and_4_out);
  and and_9 (SLT, _2, not_14_out, not_15_out, and_4_out);
  and and_10 (NOR, _2, not_16_out, _0, and_4_out);
endmodule

module AND (
  input  [31:0] A,
  input  [31:0] B,
  output [31:0] \output 
);

  and and_1 (\output [31], B[31], A[31]);
  and and_2 (\output [30], B[30], A[30]);
  and and_3 (\output [29], B[29], A[29]);
  and and_4 (\output [28], B[28], A[28]);
  and and_5 (\output [27], B[27], A[27]);
  and and_6 (\output [25], B[25], A[25]);
  and and_7 (\output [26], B[26], A[26]);
  and and_8 (\output [23], B[23], A[23]);
  and and_9 (\output [24], B[24], A[24]);
  and and_10 (\output [21], B[21], A[21]);
  and and_11 (\output [22], B[22], A[22]);
  and and_12 (\output [20], B[20], A[20]);
  and and_13 (\output [19], B[19], A[19]);
  and and_14 (\output [17], B[17], A[17]);
  and and_15 (\output [18], B[18], A[18]);
  and and_16 (\output [15], B[15], A[15]);
  and and_17 (\output [16], B[16], A[16]);
  and and_18 (\output [13], B[13], A[13]);
  and and_19 (\output [14], B[14], A[14]);
  and and_20 (\output [12], B[12], A[12]);
  and and_21 (\output [11], B[11], A[11]);
  and and_22 (\output [10], B[10], A[10]);
  and and_23 (\output [9], B[9], A[9]);
  and and_24 (\output [7], B[7], A[7]);
  and and_25 (\output [8], B[8], A[8]);
  and and_26 (\output [6], B[6], A[6]);
  and and_27 (\output [5], B[5], A[5]);
  and and_28 (\output [3], B[3], A[3]);
  and and_29 (\output [4], B[4], A[4]);
  and and_30 (\output [1], B[1], A[1]);
  and and_31 (\output [2], B[2], A[2]);
  and and_32 (\output [0], B[0], A[0]);
endmodule

module OR (
  input  [31:0] A,
  input  [31:0] B,
  output [31:0] \output 
);

  or or_1 (\output [31], B[31], A[31]);
  or or_2 (\output [29], B[29], A[29]);
  or or_3 (\output [30], B[30], A[30]);
  or or_4 (\output [27], B[27], A[27]);
  or or_5 (\output [28], B[28], A[28]);
  or or_6 (\output [26], B[26], A[26]);
  or or_7 (\output [25], B[25], A[25]);
  or or_8 (\output [23], B[23], A[23]);
  or or_9 (\output [24], B[24], A[24]);
  or or_10 (\output [21], B[21], A[21]);
  or or_11 (\output [22], B[22], A[22]);
  or or_12 (\output [20], B[20], A[20]);
  or or_13 (\output [19], B[19], A[19]);
  or or_14 (\output [17], B[17], A[17]);
  or or_15 (\output [18], B[18], A[18]);
  or or_16 (\output [15], B[15], A[15]);
  or or_17 (\output [16], B[16], A[16]);
  or or_18 (\output [14], B[14], A[14]);
  or or_19 (\output [13], B[13], A[13]);
  or or_20 (\output [12], B[12], A[12]);
  or or_21 (\output [11], B[11], A[11]);
  or or_22 (\output [9], B[9], A[9]);
  or or_23 (\output [10], B[10], A[10]);
  or or_24 (\output [8], B[8], A[8]);
  or or_25 (\output [7], B[7], A[7]);
  or or_26 (\output [5], B[5], A[5]);
  or or_27 (\output [6], B[6], A[6]);
  or or_28 (\output [4], B[4], A[4]);
  or or_29 (\output [3], B[3], A[3]);
  or or_30 (\output [2], B[2], A[2]);
  or or_31 (\output [1], B[1], A[1]);
  or or_32 (\output [0], B[0], A[0]);
endmodule

module NOR (
  input  [31:0] A,
  input  [31:0] B,
  output [31:0] \output 
);

  nor nor_1 (\output [31], B[31], A[31]);
  nor nor_2 (\output [29], B[29], A[29]);
  nor nor_3 (\output [30], B[30], A[30]);
  nor nor_4 (\output [28], B[28], A[28]);
  nor nor_5 (\output [27], B[27], A[27]);
  nor nor_6 (\output [25], B[25], A[25]);
  nor nor_7 (\output [26], B[26], A[26]);
  nor nor_8 (\output [24], B[24], A[24]);
  nor nor_9 (\output [23], B[23], A[23]);
  nor nor_10 (\output [22], B[22], A[22]);
  nor nor_11 (\output [21], B[21], A[21]);
  nor nor_12 (\output [19], B[19], A[19]);
  nor nor_13 (\output [20], B[20], A[20]);
  nor nor_14 (\output [17], B[17], A[17]);
  nor nor_15 (\output [18], B[18], A[18]);
  nor nor_16 (\output [15], B[15], A[15]);
  nor nor_17 (\output [16], B[16], A[16]);
  nor nor_18 (\output [13], B[13], A[13]);
  nor nor_19 (\output [14], B[14], A[14]);
  nor nor_20 (\output [12], B[12], A[12]);
  nor nor_21 (\output [11], B[11], A[11]);
  nor nor_22 (\output [9], B[9], A[9]);
  nor nor_23 (\output [10], B[10], A[10]);
  nor nor_24 (\output [7], B[7], A[7]);
  nor nor_25 (\output [8], B[8], A[8]);
  nor nor_26 (\output [6], B[6], A[6]);
  nor nor_27 (\output [5], B[5], A[5]);
  nor nor_28 (\output [3], B[3], A[3]);
  nor nor_29 (\output [4], B[4], A[4]);
  nor nor_30 (\output [2], B[2], A[2]);
  nor nor_31 (\output [1], B[1], A[1]);
  nor nor_32 (\output [0], B[0], A[0]);
endmodule

module ALU (
  input  _2,
  input  _1,
  input  _0,
  input  [31:0] B,
  input  [31:0] A,
  output over_flow,
  output [31:0] \output 
);

  wire ADD_overflow, SUB_overflow;
  wire [0:0] comparator_1_lt;
  wire [30:0] bits;
  wire [31:0] ADD_output, AND_output, nor_1_output, OR_output, SUB_output;

  AND AND (.A(A), .B(B), .\output (AND_output));
  OR OR (.A(A), .B(B), .\output (OR_output));
  NOR nor_1 (.A(A), .B(B), .\output (nor_1_output));
  ADD ADD (.A(A), .B(B), .Output(ADD_output), .Overflow(ADD_overflow));
  SUB SUB (.A(A), .B(B), .Output(SUB_output), .Overflow(SUB_overflow));
  Comparator #(.width(32)) comparator_1 (.a(A), .b(B), .lt(comparator_1_lt[0]));  // open: gt, eq
  or or_2 (over_flow, ADD_overflow, SUB_overflow);
  Multiplexer #(.select(3), .width(32), .enable("false")) multiplexer_1 (
    .in0(ADD_output), .in1(SUB_output), .in2(AND_output), .in3(OR_output), .in4({bits, comparator_1_lt[0]}),
    .in5(nor_1_output), .out(\output ), .sel({_2, _1, _0}));  // open: in6, in7
  Register #(.width(31)) register_1 (.Q(bits));  // open: D, en, clk, clr
endmodule

module ADD (
  input  [31:0] A,
  input  [31:0] B,
  output [31:0] Output,
  output Overflow
);

  wire not_1_out, xor_1_out, xor_2_out;

  // Probe on A
  // Probe on B
  Adder #(.width(32)) adder_1 (.a(A), .b(B), .out(Output));  // open: cin, cout
  // Probe on Output
  xor xor_1 (xor_1_out, A[31], B[31]);
  xor xor_2 (xor_2_out, Output[31], A[31]);
  not not_1 (not_1_out, xor_1_out);
  and and_1 (Overflow, xor_2_out, not_1_out);
endmodule

module SUB (
  input  [31:0] A,
  input  [31:0] B,
  output [31:0] Output,
  output Overflow
);

  wire xor_1_out, xor_2_out;

  // Probe on A
  // Probe on B
  Subtractor #(.width(32)) subtractor_1 (.a(A), .b(B), .out(Output));  // open: bin, bout
  // Probe on Output
  xor xor_1 (xor_1_out, A[31], B[31]);
  xor xor_2 (xor_2_out, Output[31], A[31]);
  and and_1 (Overflow, xor_2_out, xor_1_out);
endmodule

module Register_set (
  input  [4:0] Rs,
  input  [4:0] Rt,
  input  [4:0] Rd,
  input  [31:0] W_bus,
  input  RegWrite,
  input  Clock,
  output [31:0] Rs_2,
  output [31:0] Rt_2
);

  wire and_1_out, and_2_out, and_3_out, and_4_out, and_5_out, and_6_out, and_7_out, and_8_out, and_9_out,
       and_10_out, and_11_out, and_12_out, and_13_out, and_14_out, and_15_out, and_16_out, and_17_out,
       and_18_out, and_19_out, and_20_out, and_21_out, and_22_out, and_23_out, and_24_out, and_25_out,
       and_26_out, and_27_out, and_28_out, and_29_out, and_30_out, and_31_out, decoder_1_out1,
       decoder_1_out2, decoder_1_out3, decoder_1_out4, decoder_1_out5, decoder_1_out6, decoder_1_out7,
       decoder_1_out8, decoder_1_out9, decoder_1_out10, decoder_1_out11, decoder_1_out12, decoder_1_out13,
       decoder_1_out14, decoder_1_out15, decoder_1_out16, decoder_1_out17, decoder_1_out18, decoder_1_out19,
       decoder_1_out20, decoder_1_out21, decoder_1_out22, decoder_1_out23, decoder_1_out24, decoder_1_out25,
       decoder_1_out26, decoder_1_out27, decoder_1_out28, decoder_1_out29, decoder_1_out30, decoder_1_out31,
       decoder_2_out0, decoder_2_out1, decoder_2_out2, decoder_2_out3, decoder_2_out4, decoder_2_out5,
       decoder_2_out6, decoder_2_out7, decoder_2_out8, decoder_2_out9, decoder_2_out10, decoder_2_out11,
       decoder_2_out12, decoder_2_out13, decoder_2_out14, decoder_2_out15, decoder_2_out16, decoder_2_out17,
       decoder_2_out18, decoder_2_out19, decoder_2_out20, decoder_2_out21, decoder_2_out22, decoder_2_out23,
       decoder_2_out24, decoder_2_out25, decoder_2_out26, decoder_2_out27, decoder_2_out28, decoder_2_out29,
       decoder_2_out30, decoder_2_out31, decoder_3_out0, decoder_3_out1, decoder_3_out2, decoder_3_out3,
       decoder_3_out4, decoder_3_out5, decoder_3_out6, decoder_3_out7, decoder_3_out8, decoder_3_out9,
       decoder_3_out10, decoder_3_out11, decoder_3_out12, decoder_3_out13, decoder_3_out14, decoder_3_out15,
       decoder_3_out16, decoder_3_out17, decoder_3_out18, decoder_3_out19, decoder_3_out20, decoder_3_out21,
       decoder_3_out22, decoder_3_out23, decoder_3_out24, decoder_3_out25, decoder_3_out26, decoder_3_out27,
       decoder_3_out28, decoder_3_out29, decoder_3_out30, decoder_3_out31;
  wire [31:0] R1_q, R2_q, R3_q, R4_q, R5_q, R6_q, R7_q, R8_q, R9_q, R10_q, R11_q, R12_q, R13_q, R14_q, R15_q,
       R16_q, R17_q, R18_q, R19_q, R20_q, R21_q, R22_q, R23_q, R24_q, R25_q, R26_q, R27_q, R28_q, R29_q,
       R30_q, R31_q;

  Decoder #(.select(5), .enable("false")) decoder_1 (
    .out1(decoder_1_out1), .out2(decoder_1_out2), .out3(decoder_1_out3), .out4(decoder_1_out4),
    .out5(decoder_1_out5), .out6(decoder_1_out6), .out7(decoder_1_out7), .out8(decoder_1_out8),
    .out9(decoder_1_out9), .out10(decoder_1_out10), .out11(decoder_1_out11), .out12(decoder_1_out12),
    .out13(decoder_1_out13), .out14(decoder_1_out14), .out15(decoder_1_out15), .out16(decoder_1_out16),
    .out17(decoder_1_out17), .out18(decoder_1_out18), .out19(decoder_1_out19), .out20(decoder_1_out20),
    .out21(decoder_1_out21), .out22(decoder_1_out22), .out23(decoder_1_out23), .out24(decoder_1_out24),
    .out25(decoder_1_out25), .out26(decoder_1_out26), .out27(decoder_1_out27), .out28(decoder_1_out28),
    .out29(decoder_1_out29), .out30(decoder_1_out30), .out31(decoder_1_out31), .sel(Rd));  // open: out0
  and and_1 (and_1_out, decoder_1_out1, RegWrite);
  and and_2 (and_2_out, decoder_1_out2, RegWrite);
  and and_3 (and_3_out, decoder_1_out3, RegWrite);
  and and_4 (and_4_out, decoder_1_out4, RegWrite);
  and and_5 (and_5_out, decoder_1_out5, RegWrite);
  and and_6 (and_6_out, decoder_1_out6, RegWrite);
  and and_7 (and_7_out, decoder_1_out7, RegWrite);
  and and_8 (and_8_out, decoder_1_out8, RegWrite);
  and and_9 (and_9_out, decoder_1_out9, RegWrite);
  and and_10 (and_10_out, decoder_1_out10, RegWrite);
  and and_11 (and_11_out, decoder_1_out11, RegWrite);
  and and_12 (and_12_out, decoder_1_out12, RegWrite);
  and and_13 (and_13_out, decoder_1_out13, RegWrite);
  and and_14 (and_14_out, decoder_1_out14, RegWrite);
  and and_15 (and_15_out, decoder_1_out15, RegWrite);
  and and_16 (and_16_out, decoder_1_out16, RegWrite);
  and and_17 (and_17_out, decoder_1_out17, RegWrite);
  and and_18 (and_18_out, decoder_1_out18, RegWrite);
  and and_19 (and_19_out, decoder_1_out19, RegWrite);
  and and_20 (and_20_out, decoder_1_out20, RegWrite);
  and and_21 (and_21_out, decoder_1_out21, RegWrite);
  and and_22 (and_22_out, decoder_1_out22, RegWrite);
  and and_23 (and_23_out, decoder_1_out23, RegWrite);
  and and_24 (and_24_out, decoder_1_out24, RegWrite);
  and and_25 (and_25_out, decoder_1_out25, RegWrite);
  and and_26 (and_26_out, decoder_1_out26, RegWrite);
  and and_27 (and_27_out, decoder_1_out27, RegWrite);
  and and_28 (and_28_out, decoder_1_out28, RegWrite);
  and and_29 (and_29_out, decoder_1_out29, RegWrite);
  and and_30 (and_30_out, decoder_1_out30, RegWrite);
  and and_31 (and_31_out, decoder_1_out31, RegWrite);
  Register #(.width(32)) R1 (.D(W_bus), .en(and_1_out), .Q(R1_q), .clk(Clock));  // open: clr
  Register #(.width(32)) R2 (.D(W_bus), .en(and_2_out), .Q(R2_q), .clk(Clock));  // open: clr
  Register #(.width(32)) R3 (.D(W_bus), .en(and_3_out), .Q(R3_q), .clk(Clock));  // open: clr
  Register #(.width(32)) R4 (.D(W_bus), .en(and_4_out), .Q(R4_q), .clk(Clock));  // open: clr
  Register #(.width(32)) R5 (.D(W_bus), .en(and_5_out), .Q(R5_q), .clk(Clock));  // open: clr
  Register #(.width(32)) R6 (.D(W_bus), .en(and_6_out), .Q(R6_q), .clk(Clock));  // open: clr
  Register #(.width(32)) R7 (.D(W_bus), .en(and_7_out), .Q(R7_q), .clk(Clock));  // open: clr
  Register #(.width(32)) R8 (.D(W_bus), .en(and_8_out), .Q(R8_q), .clk(Clock));  // open: clr
  Register #(.width(32)) R9 (.D(W_bus), .en(and_9_out), .Q(R9_q), .clk(Clock));  // open: clr
  Register #(.width(32)) R10 (.D(W_bus), .en(and_10_out), .Q(R10_q), .clk(Clock));  // open: clr
  Register #(.width(32)) R11 (.D(W_bus), .en(and_11_out), .Q(R11_q), .clk(Clock));  // open: clr
  Register #(.width(32)) R12 (.D(W_bus), .en(and_12_out), .Q(R12_q), .clk(Clock));  // open: clr
  Register #(.width(32)) R13 (.D(W_bus), .en(and_13_out), .Q(R13_q), .clk(Clock));  // open: clr
  Register #(.width(32)) R14 (.D(W_bus), .en(and_14_out), .Q(R14_q), .clk(Clock));  // open: clr
  Register #(.width(32)) R15 (.D(W_bus), .en(and_15_out), .Q(R15_q), .clk(Clock));  // open: clr
  Register #(.width(32)) R16 (.D(W_bus), .en(and_16_out), .Q(R16_q), .clk(Clock));  // open: clr
  Register #(.width(32)) R17 (.D(W_bus), .en(and_17_out), .Q(R17_q), .clk(Clock));  // open: clr
  Register #(.width(32)) R18 (.D(W_bus), .en(and_18_out), .Q(R18_q), .clk(Clock));  // open: clr
  Register #(.width(32)) R19 (.D(W_bus), .en(and_19_out), .Q(R19_q), .clk(Clock));  // open: clr
  Register #(.width(32)) R20 (.D(W_bus), .en(and_20_out), .Q(R20_q), .clk(Clock));  // open: clr
  Register #(.width(32)) R21 (.D(W_bus), .en(and_21_out), .Q(R21_q), .clk(Clock));  // open: clr
  Register #(.width(32)) R22 (.D(W_bus), .en(and_22_out), .Q(R22_q), .clk(Clock));  // open: clr
  Register #(.width(32)) R23 (.D(W_bus), .en(and_23_out), .Q(R23_q), .clk(Clock));  // open: clr
  Register #(.width(32)) R24 (.D(W_bus), .en(and_24_out), .Q(R24_q), .clk(Clock));  // open: clr
  Register #(.width(32)) R25 (.D(W_bus), .en(and_25_out), .Q(R25_q), .clk(Clock));  // open: clr
  Register #(.width(32)) R26 (.D(W_bus), .en(and_26_out), .Q(R26_q), .clk(Clock));  // open: clr
  Register #(.width(32)) R27 (.D(W_bus), .en(and_27_out), .Q(R27_q), .clk(Clock));  // open: clr
  Register #(.width(32)) R28 (.D(W_bus), .en(and_28_out), .Q(R28_q), .clk(Clock));  // open: clr
  Register #(.width(32)) R29 (.D(W_bus), .en(and_29_out), .Q(R29_q), .clk(Clock));  // open: clr
  Register #(.width(32)) R30 (.D(W_bus), .en(and_30_out), .Q(R30_q), .clk(Clock));  // open: clr
  Register #(.width(32)) R31 (.D(W_bus), .en(and_31_out), .Q(R31_q), .clk(Clock));  // open: clr
  assign Rs_2 = decoder_2_out1 ? R1_q : 32'bz;  // Controlled_Buffer controlled_buffer_1
  assign Rs_2 = decoder_2_out2 ? R2_q : 32'bz;  // Controlled_Buffer controlled_buffer_2
  assign Rs_2 = decoder_2_out3 ? R3_q : 32'bz;  // Controlled_Buffer controlled_buffer_3
  assign Rs_2 = decoder_2_out4 ? R4_q : 32'bz;  // Controlled_Buffer controlled_buffer_4
  assign Rs_2 = decoder_2_out5 ? R5_q : 32'bz;  // Controlled_Buffer controlled_buffer_5
  assign Rs_2 = decoder_2_out6 ? R6_q : 32'bz;  // Controlled_Buffer controlled_buffer_6
  assign Rs_2 = decoder_2_out7 ? R7_q : 32'bz;  // Controlled_Buffer controlled_buffer_7
  assign Rs_2 = decoder_2_out8 ? R8_q : 32'bz;  // Controlled_Buffer controlled_buffer_8
  assign Rs_2 = decoder_2_out9 ? R9_q : 32'bz;  // Controlled_Buffer controlled_buffer_9
  assign Rs_2 = decoder_2_out10 ? R10_q : 32'bz;  // Controlled_Buffer controlled_buffer_10
  assign Rs_2 = decoder_2_out11 ? R11_q : 32'bz;  // Controlled_Buffer controlled_buffer_11
  assign Rs_2 = decoder_2_out12 ? R12_q : 32'bz;  // Controlled_Buffer controlled_buffer_12
  assign Rs_2 = decoder_2_out13 ? R13_q : 32'bz;  // Controlled_Buffer controlled_buffer_13
  assign Rs_2 = decoder_2_out14 ? R14_q : 32'bz;  // Controlled_Buffer controlled_buffer_14
  assign Rs_2 = decoder_2_out15 ? R15_q : 32'bz;  // Controlled_Buffer controlled_buffer_15
  assign Rs_2 = decoder_2_out16 ? R16_q : 32'bz;  // Controlled_Buffer controlled_buffer_16
  assign Rs_2 = decoder_2_out17 ? R17_q : 32'bz;  // Controlled_Buffer controlled_buffer_17
  assign Rs_2 = decoder_2_out18 ? R18_q : 32'bz;  // Controlled_Buffer controlled_buffer_18
  assign Rs_2 = decoder_2_out19 ? R19_q : 32'bz;  // Controlled_Buffer controlled_buffer_19
  assign Rs_2 = decoder_2_out20 ? R20_q : 32'bz;  // Controlled_Buffer controlled_buffer_20
  assign Rs_2 = decoder_2_out21 ? R21_q : 32'bz;  // Controlled_Buffer controlled_buffer_21
  assign Rs_2 = decoder_2_out22 ? R22_q : 32'bz;  // Controlled_Buffer controlled_buffer_22
  assign Rs_2 = decoder_2_out23 ? R23_q : 32'bz;  // Controlled_Buffer controlled_buffer_23
  assign Rs_2 = decoder_2_out24 ? R24_q : 32'bz;  // Controlled_Buffer controlled_buffer_24
  assign Rs_2 = decoder_2_out25 ? R25_q : 32'bz;  // Controlled_Buffer controlled_buffer_25
  assign Rs_2 = decoder_2_out26 ? R26_q : 32'bz;  // Controlled_Buffer controlled_buffer_26
  assign Rs_2 = decoder_2_out27 ? R27_q : 32'bz;  // Controlled_Buffer controlled_buffer_27
  assign Rs_2 = decoder_2_out28 ? R28_q : 32'bz;  // Controlled_Buffer controlled_buffer_28
  assign Rs_2 = decoder_2_out29 ? R29_q : 32'bz;  // Controlled_Buffer controlled_buffer_29
  assign Rs_2 = decoder_2_out30 ? R30_q : 32'bz;  // Controlled_Buffer controlled_buffer_30
  assign Rs_2 = decoder_2_out31 ? R31_q : 32'bz;  // Controlled_Buffer controlled_buffer_31
  assign Rs_2 = decoder_2_out0 ? {32{1'b0}} : 32'bz;  // Controlled_Buffer controlled_buffer_32
  Decoder #(.select(5), .enable("false")) decoder_2 (
    .out0(decoder_2_out0), .out1(decoder_2_out1), .out2(decoder_2_out2), .out3(decoder_2_out3),
    .out4(decoder_2_out4), .out5(decoder_2_out5), .out6(decoder_2_out6), .out7(decoder_2_out7),
    .out8(decoder_2_out8), .out9(decoder_2_out9), .out10(decoder_2_out10), .out11(decoder_2_out11),
    .out12(decoder_2_out12), .out13(decoder_2_out13), .out14(decoder_2_out14), .out15(decoder_2_out15),
    .out16(decoder_2_out16), .out17(decoder_2_out17), .out18(decoder_2_out18), .out19(decoder_2_out19),
    .out20(decoder_2_out20), .out21(decoder_2_out21), .out22(decoder_2_out22), .out23(decoder_2_out23),
    .out24(decoder_2_out24), .out25(decoder_2_out25), .out26(decoder_2_out26), .out27(decoder_2_out27),
    .out28(decoder_2_out28), .out29(decoder_2_out29), .out30(decoder_2_out30), .out31(decoder_2_out31),
    .sel(Rs));
  assign Rt_2 = decoder_3_out1 ? R1_q : 32'bz;  // Controlled_Buffer controlled_buffer_33
  assign Rt_2 = decoder_3_out2 ? R2_q : 32'bz;  // Controlled_Buffer controlled_buffer_34
  assign Rt_2 = decoder_3_out3 ? R3_q : 32'bz;  // Controlled_Buffer controlled_buffer_35
  assign Rt_2 = decoder_3_out4 ? R4_q : 32'bz;  // Controlled_Buffer controlled_buffer_36
  assign Rt_2 = decoder_3_out5 ? R5_q : 32'bz;  // Controlled_Buffer controlled_buffer_37
  assign Rt_2 = decoder_3_out6 ? R6_q : 32'bz;  // Controlled_Buffer controlled_buffer_38
  assign Rt_2 = decoder_3_out7 ? R7_q : 32'bz;  // Controlled_Buffer controlled_buffer_39
  assign Rt_2 = decoder_3_out8 ? R8_q : 32'bz;  // Controlled_Buffer controlled_buffer_40
  assign Rt_2 = decoder_3_out9 ? R9_q : 32'bz;  // Controlled_Buffer controlled_buffer_41
  assign Rt_2 = decoder_3_out10 ? R10_q : 32'bz;  // Controlled_Buffer controlled_buffer_42
  assign Rt_2 = decoder_3_out11 ? R11_q : 32'bz;  // Controlled_Buffer controlled_buffer_43
  assign Rt_2 = decoder_3_out12 ? R12_q : 32'bz;  // Controlled_Buffer controlled_buffer_44
  assign Rt_2 = decoder_3_out13 ? R13_q : 32'bz;  // Controlled_Buffer controlled_buffer_45
  assign Rt_2 = decoder_3_out14 ? R14_q : 32'bz;  // Controlled_Buffer controlled_buffer_46
  assign Rt_2 = decoder_3_out15 ? R15_q : 32'bz;  // Controlled_Buffer controlled_buffer_47
  assign Rt_2 = decoder_3_out16 ? R16_q : 32'bz;  // Controlled_Buffer controlled_buffer_48
  assign Rt_2 = decoder_3_out17 ? R17_q : 32'bz;  // Controlled_Buffer controlled_buffer_49
  assign Rt_2 = decoder_3_out18 ? R18_q : 32'bz;  // Controlled_Buffer controlled_buffer_50
  assign Rt_2 = decoder_3_out19 ? R19_q : 32'bz;  // Controlled_Buffer controlled_buffer_51
  assign Rt_2 = decoder_3_out20 ? R20_q : 32'bz;  // Controlled_Buffer controlled_buffer_52
  assign Rt_2 = decoder_3_out21 ? R21_q : 32'bz;  // Controlled_Buffer controlled_buffer_53
  assign Rt_2 = decoder_3_out22 ? R22_q : 32'bz;  // Controlled_Buffer controlled_buffer_54
  assign Rt_2 = decoder_3_out23 ? R23_q : 32'bz;  // Controlled_Buffer controlled_buffer_55
  assign Rt_2 = decoder_3_out24 ? R24_q : 32'bz;  // Controlled_Buffer controlled_buffer_56
  assign Rt_2 = decoder_3_out25 ? R25_q : 32'bz;  // Controlled_Buffer controlled_buffer_57
  assign Rt_2 = decoder_3_out26 ? R26_q : 32'bz;  // Controlled_Buffer controlled_buffer_58
  assign Rt_2 = decoder_3_out27 ? R27_q : 32'bz;  // Controlled_Buffer controlled_buffer_59
  assign Rt_2 = decoder_3_out28 ? R28_q : 32'bz;  // Controlled_Buffer controlled_buffer_60
  assign Rt_2 = decoder_3_out29 ? R29_q : 32'bz;  // Controlled_Buffer controlled_buffer_61
  assign Rt_2 = decoder_3_out30 ? R30_q : 32'bz;  // Controlled_Buffer controlled_buffer_62
  assign Rt_2 = decoder_3_out31 ? R31_q : 32'bz;  // Controlled_Buffer controlled_buffer_63
  assign Rt_2 = decoder_3_out0 ? {32{1'b0}} : 32'bz;  // Controlled_Buffer controlled_buffer_64
  Decoder #(.select(5), .enable("false")) decoder_3 (
    .out0(decoder_3_out0), .out1(decoder_3_out1), .out2(decoder_3_out2), .out3(decoder_3_out3),
    .out4(decoder_3_out4), .out5(decoder_3_out5), .out6(decoder_3_out6), .out7(decoder_3_out7),
    .out8(decoder_3_out8), .out9(decoder_3_out9), .out10(decoder_3_out10), .out11(decoder_3_out11),
    .out12(decoder_3_out12), .out13(decoder_3_out13), .out14(decoder_3_out14), .out15(decoder_3_out15),
    .out16(decoder_3_out16), .out17(decoder_3_out17), .out18(decoder_3_out18), .out19(decoder_3_out19),
    .out20(decoder_3_out20), .out21(decoder_3_out21), .out22(decoder_3_out22), .out23(decoder_3_out23),
    .out24(decoder_3_out24), .out25(decoder_3_out25), .out26(decoder_3_out26), .out27(decoder_3_out27),
    .out28(decoder_3_out28), .out29(decoder_3_out29), .out30(decoder_3_out30), .out31(decoder_3_out31),
    .sel(Rt));

  // Notes on the sheet:
  //   Bus W
  //   Bus A
  //   Bus B
endmodule
