// Logisim project B22CS068A.circ as structural Verilog: 1 circuit, main circuit main
module main (
  input  b31,
  input  b30,
  input  b29,
  input  b28,
  input  b27,
  input  b26,
  input  [31:0] Instruction,
  input  in_8,
  input  in_9,
  input  in_10,
  input  in_11,
  output RegDest,
  output JUMP,
  output ALUSrc,
  output ALUNeeded,
  output MemToReg,
  output Addi,
  output lw,
  output sw,
  output RegWrite,
  output MemRead,
  output MemWrite,
  output beq,
  output Branch,
  output Add,
  output Sub,
  output ALUOp1,
  output AND,
  output OR,
  output Slt,
  output ALUOp0
);

  wire and_2_out, and_3_out, decoder_1_out0, decoder_1_out1, decoder_1_out2, not_1_out, not_2_out, not_3_out,
       not_4_out, not_5_out, not_6_out, not_7_out, not_8_out, not_9_out;

  not not_1 (not_1_out, b29);
  not not_2 (not_2_out, b27);
  not not_3 (not_3_out, b28);
  not not_4 (not_4_out, b27);
  not not_5 (not_5_out, b29);
  not not_6 (not_6_out, b29);
  not not_7 (not_7_out, b29);
  not not_8 (not_8_out, b28);
  not not_9 (not_9_out, b27);
  and and_1 (RegDest, not_1_out, not_2_out);
  and and_2 (and_2_out, not_3_out, not_4_out);
  and and_3 (and_3_out, b31, not_5_out);
  and and_4 (MemRead, b31, not_6_out);
  and and_5 (MemWrite, b31, b29);
  or or_1 (ALUSrc, b27, b29);
  or or_2 (RegWrite, and_2_out, and_3_out);
  and and_6 (ALUOp1, not_7_out, not_8_out, not_9_out);
  Decoder #(.select(2), .enable("false")) decoder_1 (
    .out0(decoder_1_out0), .out1(decoder_1_out1), .out2(decoder_1_out2), .sel({ALUOp1, b28}));  // open: out3
  Demultiplexer #(.select(4), .enable("false")) demultiplexer_1 (
    .out0(Add), .out2(Sub), .out4(AND), .out5(OR), .out10(Slt), .in(decoder_1_out2),
    .sel({in_8, in_9, in_10, in_11}));  // open: out1, out3, out6, out7, out8, out9, out11, out12, out13, out14, out15
  Demultiplexer #(.select(2), .enable("false")) demultiplexer_2 (
    .out1(Addi), .out2(lw), .out3(sw), .in(decoder_1_out0), .sel({b31, b29}));  // open: out0
  and and_7 (JUMP, decoder_1_out0, b27);
  and and_8 (beq, decoder_1_out1, b28);
  not not_10 (ALUNeeded, JUMP);

  assign ALUOp0 = b28;
  assign Branch = b28;
  assign MemToReg = b27;

  // Other names for the same wires on the sheet: op2 = b28; f0 = in_11; f1 = in_10; f2 = in_9; f3 = in_8; op3 = b29;
  //   op5 = b31; op0 = b26; op1 = b27; op4 = b30
endmodule
