// Logisim project logisim_Assign.circ as structural Verilog: 1 circuit, main circuit main
module main (
  input  b31,
  input  b26,
  output MemRead,
  output ALUOp1,
  output AND,
  output Slt,
  output ALUOp0
);

  wire not_2_out, not_3_out, not_4_out, or_1_p1, or_1_p3, undriven, undriven_2, undriven_3;

  // NOT_Gate not_1 has open pins: in=undriven, out=open
  not not_2 (not_2_out, undriven_2);
  not not_3 (not_3_out, undriven_3);
  // NOT_Gate not_4 has open pins: in=open, out=not_4_out
  // OR_Gate or_1: pin names not known; wires that end beside it: or_1_p1, or_1_p1, or_1_p3, or_1_p3
endmodule
